# Fritzing sketch layout (saved by Fritzing 0.9.2b)

parts:
  Part2 = NRF24L01
  J1 = Basic Servo
  Part3 = Arduino Uno (Rev3) - ICSP

nets:
  N1: Part2.MOSI, Part3.ICSP_MOSI, Part3.D11_PWM/MOSI
  N2: Part2.CSN, Part3.D10_PWM/SS
  VCC: Part2.VCC, Part3.3V3
  N3: Part2.MISO, Part3.ICSP_MISO, Part3.D12/MISO
  N4: Part2.SCK, Part3.ICSP_SCK, Part3.D13/SCK
  N5: Part2.CE, Part3.D9_PWM
  GND: Part2.GND, J1.gnd, Part3.GND
  VCC_2: J1.vcc, Part3.5V
  N6: J1.pulse, Part3.D6_PWM
