# Fritzing sketch layout (saved by Fritzing 0.9.2b)
breadboards: 1

parts:
  Part1 = Arduino Nano (Rev3.0)
  S1 = Pushbutton [package="[THT]"]
  S2 = Pushbutton [package="[THT]"]
  R1 = Resistor [tolerance=±5% resistance=10k package=THT]
  R2 = Resistor [tolerance=±5% resistance=10k package=THT]
  Part2 = NRF24L01
  Part3 = Breadboard Power Supply Board SMD

nets:
  GND: Part1.GND, R1.Pin_1, R2.Pin_1, Part2.GND, Part3.GND
  N1: Part1.D5, Part1.D6, Part1.A7, S1.Pin_1, S1.Pin_2, S1.Pin_3, S1.Pin_4, S2.Pin_1, S2.Pin_2, S2.Pin_3, S2.Pin_4, R1.Pin_0, R2.Pin_0
  N2: Part1.D9, Part2.CE
  N3: Part1.D10, Part2.CSN
  N4: Part1.D11/MOSI, Part2.MOSI
  N5: Part1.D12/MISO, Part2.MISO
  N6: Part1.D13/SCK, Part2.SCK
